// Logisim project Regfile.circ as structural Verilog: 1 circuit, main circuit main
module main (
  input  [1:0] Read_register_1,
  input  [1:0] Read_register_2,
  input  [1:0] write_register,
  input  [15:0] write_data,
  input  RegWrite,
  input  clock,
  output [15:0] Reg_0_Value,
  output [15:0] Reg_1_Value,
  output [15:0] Reg_2_Value,
  output [15:0] Reg_3_Value,
  output [15:0] Read_Data_1,
  output [15:0] Read_Data_2
);

  wire Which1, Which2, Which3, Which4;
  wire [15:0] Out1, Out2, Out3, Out4;

  Register #(.width(16)) register_1 (.D(Out1), .en(Which1), .Q(Reg_0_Value), .clk(clock));  // open: clr
  Register #(.width(16)) register_2 (.D(Out2), .en(Which2), .Q(Reg_1_Value), .clk(clock));  // open: clr
  Multiplexer #(.select(2), .width(16), .enable("false")) multiplexer_1 (
    .in0(Reg_0_Value), .in1(Reg_1_Value), .in2(Reg_2_Value), .in3(Reg_3_Value), .out(Read_Data_1),
    .sel(Read_register_1));
  Multiplexer #(.select(2), .width(16), .enable("false")) multiplexer_2 (
    .in0(Reg_0_Value), .in1(Reg_1_Value), .in2(Reg_2_Value), .in3(Reg_3_Value), .out(Read_Data_2),
    .sel(Read_register_2));
  Register #(.width(16)) register_3 (.D(Out3), .en(Which3), .Q(Reg_2_Value), .clk(clock));  // open: clr
  Register #(.width(16)) register_4 (.D(Out4), .en(Which4), .Q(Reg_3_Value), .clk(clock));  // open: clr
  Demultiplexer #(.select(2), .enable("false")) demultiplexer_1 (
    .out0(Which1), .out1(Which2), .out2(Which3), .out3(Which4), .in(1'b1), .sel(write_register));
  Demultiplexer #(.select(2), .width(16)) demultiplexer_2 (
    .out0(Out1), .out1(Out2), .out2(Out3), .out3(Out4), .in(write_data), .sel(write_register), .en(RegWrite));

  // Other names for the same wires on the sheet: Reg0[15:0] = Reg_0_Value; Reg1[15:0] = Reg_1_Value;
  //   Reg2[15:0] = Reg_2_Value; Reg3[15:0] = Reg_3_Value; RReg1[1:0] = Read_register_1; RReg2[1:0] = Read_register_2;
  //   RWrite = RegWrite; WData[15:0] = write_data; WReg[1:0] = write_register

  // Notes on the sheet:
  //   These are INPUTS to the circuit
  //   These are INPUTS to the circuit
  //   DO NOT CHANGE THE LOCATIONS OF THE INPUTS/OUTPUTS! IF YOU DO SO, YOU NEED TO MAKE SURE THE PINS ARE AT THE RIGHT PLACE!
  //   These are OUTPUTS to the circuit
  //   Yet again, the clock is not an actual clock, but an input, one that will be driven from a higher circuit
  //   These are OUTPUTS to the circuit
endmodule
