// Logisim project alu.circ as structural Verilog: 7 circuits, main circuit main
module main (
  input  [15:0] X,
  input  [15:0] Y,
  input  [3:0] Switch__S,
  output Signed_Overflow,
  output [15:0] RESULT,
  output Equal
);

  wire comparator_1_lt, n8addoverflow_1_out, n8suboverflow_1_out, n16addoverflow_1_out, n16suboverflow_1_out;
  wire [15:0] adder_1_out, addp8_1_out, and_1_out, or_1_out, shifter_1_out, shifter_2_out, shifter_3_out,
       slt, subp8_1_out, subtractor_1_out;

  Comparator #(.width(16)) comparator_1 (.a(X), .b(Y), .lt(comparator_1_lt));  // open: gt, eq
  Multiplexer #(.width(16), .enable("false")) multiplexer_1 (
    .in0({16{1'b0}}), .in1(16'h1), .out(slt), .sel(comparator_1_lt));
  Adder #(.width(16)) adder_1 (.a(X), .b(Y), .out(adder_1_out));  // open: cin, cout
  Subtractor #(.width(16)) subtractor_1 (.a(X), .b(Y), .out(subtractor_1_out));  // open: bin, bout
  Shifter #(.width(16)) shifter_1 (.in(X), .\dist (Y[3:0]), .out(shifter_1_out));
  Shifter #(.width(16), .shift("lr")) shifter_2 (.in(X), .\dist (Y[3:0]), .out(shifter_2_out));
  Shifter #(.width(16), .shift("ar")) shifter_3 (.in(X), .\dist (Y[3:0]), .out(shifter_3_out));
  assign or_1_out = X | Y;  // OR_Gate or_1, 16 bits wide
  assign and_1_out = X & Y;  // AND_Gate and_1, 16 bits wide
  addp8 addp8_1 (.x(X), .y(Y), .out(addp8_1_out));
  Multiplexer #(.select(4), .width(16), .enable("false")) multiplexer_2 (
    .in0(adder_1_out), .in1(subtractor_1_out), .in2(shifter_1_out), .in3(shifter_2_out), .in4(shifter_3_out),
    .in5(slt), .in6(or_1_out), .in7(and_1_out), .in8(addp8_1_out), .in9(subp8_1_out), .out(RESULT),
    .sel(Switch__S));  // open: in10, in11, in12, in13, in14, in15
  subp8 subp8_1 (.x(X), .y(Y), .out(subp8_1_out));
  _16addoverflow u_16addoverflow_1 (.x(X), .y(Y), .out(n16addoverflow_1_out));
  _16suboverflow u_16suboverflow_1 (.x(X), .y(Y), .out(n16suboverflow_1_out));
  _8addoverflow u_8addoverflow_1 (.x(X), .y(Y), .out(n8addoverflow_1_out));
  _8suboverflow u_8suboverflow_1 (.x(X), .y(Y), .out(n8suboverflow_1_out));
  Multiplexer #(.select(4), .enable("false")) multiplexer_3 (
    .in0(n16addoverflow_1_out), .in1(n16suboverflow_1_out), .in8(n8addoverflow_1_out),
    .in9(n8suboverflow_1_out), .out(Signed_Overflow), .sel(Switch__S));  // open: in2, in3, in4, in5, in6, in7, in10, in11, in12, in13, in14, in15
  Comparator #(.width(16)) comparator_2 (.a(X), .b(Y), .eq(Equal));  // open: gt, lt

  // Other names for the same wires on the sheet: so = Signed_Overflow; sw[3:0] = Switch__S; _4bit[3:0] = Y[3:0]

  // Notes on the sheet:
  //   INPUTS to your circuit
  //   INPUT to your circuit
  //   DON'T CHANGE THE INPUTS AND OUTPUTS! IF YOU DO SO, YOU NEED TO MAKE SURE THE PINS ARE IN THE RIGHT PLACES!
  //   OUTPUTS of your circuit
endmodule

module addp8 (
  input  [15:0] x,
  input  [15:0] y,
  output [15:0] out
);

  Adder adder_1 (.a(x[7:0]), .b(y[7:0]), .out(out[7:0]));  // open: cin, cout
  Adder adder_2 (.a(x[15:8]), .b(y[15:8]), .out(out[15:8]));  // open: cin, cout

  // Other names for the same wires on the sheet: xsecond8[7:0] = x[7:0]; xfirst8[7:0] = x[15:8];
  //   ysecond8[7:0] = y[7:0]; yfirst8[7:0] = y[15:8]
endmodule

module subp8 (
  input  [15:0] x,
  input  [15:0] y,
  output [15:0] out
);

  Subtractor subtractor_1 (.a(x[7:0]), .b(y[7:0]), .out(out[7:0]));  // open: bin, bout
  Subtractor subtractor_2 (.a(x[15:8]), .b(y[15:8]), .out(out[15:8]));  // open: bin, bout

  // Other names for the same wires on the sheet: xsecond8[7:0] = x[7:0]; xfirst8[7:0] = x[15:8];
  //   ysecond8[7:0] = y[7:0]; yfirst8[7:0] = y[15:8]
endmodule

module _16addoverflow (
  input  [15:0] x,
  input  [15:0] y,
  output out
);

  wire and_1_out, and_2_out, notplusbit, notxbit, notybit, plusbit;
  wire [14:0] adder_1_out;

  Adder #(.width(16)) adder_1 (.a(x), .b(y), .out({plusbit, adder_1_out}));  // open: cin, cout
  not not_1 (notxbit, x[15]);
  not not_2 (notybit, y[15]);
  not not_3 (notplusbit, plusbit);
  and and_1 (and_1_out, notxbit, plusbit, notybit);
  and and_2 (and_2_out, x[15], notplusbit, y[15]);
  or or_1 (out, and_1_out, and_2_out);

  // Other names for the same wires on the sheet: xbit = x[15]; ybit = y[15]
endmodule

module _16suboverflow (
  input  [15:0] x,
  input  [15:0] y,
  output out
);

  wire and_1_out, and_2_out, minusbit, notminusbit, notxbit, notybit;
  wire [14:0] subtractor_1_out;

  Subtractor #(.width(16)) subtractor_1 (.a(x), .b(y), .out({minusbit, subtractor_1_out}));  // open: bin, bout
  not not_1 (notxbit, x[15]);
  not not_2 (notybit, y[15]);
  not not_3 (notminusbit, minusbit);
  and and_1 (and_1_out, notxbit, minusbit, y[15]);
  and and_2 (and_2_out, x[15], notminusbit, notybit);
  or or_1 (out, and_1_out, and_2_out);

  // Other names for the same wires on the sheet: xbit = x[15]; ybit = y[15]
endmodule

module _8addoverflow (
  input  [15:0] x,
  input  [15:0] y,
  output out
);

  wire and_1_out, and_2_out, and_3_out, and_4_out, notplusbit1, notplusbit2, notxbit1, notxbit2, notybit1,
       notybit2, plusbit1, plusbit2;
  wire [6:0] adder_1_out, adder_2_out;

  Adder adder_1 (.a(x[15:8]), .b(y[15:8]), .out({plusbit1, adder_1_out}));  // open: cin, cout
  not not_1 (notplusbit1, plusbit1);
  Adder adder_2 (.a(x[7:0]), .b(y[7:0]), .out({plusbit2, adder_2_out}));  // open: cin, cout
  not not_2 (notxbit1, x[15]);
  not not_3 (notxbit2, x[7]);
  not not_4 (notybit1, y[15]);
  not not_5 (notybit2, y[7]);
  not not_6 (notplusbit2, plusbit2);
  and and_1 (and_1_out, notxbit1, plusbit1, notybit1);
  and and_2 (and_2_out, x[15], notplusbit1, y[15]);
  and and_3 (and_3_out, notxbit2, plusbit2, notybit2);
  and and_4 (and_4_out, x[7], notplusbit2, y[7]);
  or or_1 (out, and_1_out, and_2_out, and_3_out, and_4_out);

  // Other names for the same wires on the sheet: xsecond8[7:0] = x[7:0]; xbit2 = x[7]; xfirst8[7:0] = x[15:8];
  //   xbit1 = x[15]; ysecond8[7:0] = y[7:0]; ybit2 = y[7]; yfirst8[7:0] = y[15:8]; ybit1 = y[15]
endmodule

module _8suboverflow (
  input  [15:0] x,
  input  [15:0] y,
  output out
);

  wire and_1_out, and_2_out, and_3_out, and_4_out, minusbit1, minusbit2, notminusbit1, notminusbit2,
       notxbit1, notxbit2, notybit1, notybit2;
  wire [6:0] subtractor_1_out, subtractor_2_out;

  Subtractor subtractor_1 (.a(x[15:8]), .b(y[15:8]), .out({minusbit1, subtractor_1_out}));  // open: bin, bout
  not not_1 (notminusbit1, minusbit1);
  Subtractor subtractor_2 (.a(x[7:0]), .b(y[7:0]), .out({minusbit2, subtractor_2_out}));  // open: bin, bout
  not not_2 (notxbit1, x[15]);
  not not_3 (notxbit2, x[7]);
  not not_4 (notybit1, y[15]);
  not not_5 (notybit2, y[7]);
  not not_6 (notminusbit2, minusbit2);
  and and_1 (and_1_out, notxbit1, minusbit1, y[15]);
  and and_2 (and_2_out, x[15], notminusbit1, notybit1);
  and and_3 (and_3_out, notxbit2, minusbit2, y[7]);
  and and_4 (and_4_out, x[7], notminusbit2, notybit2);
  or or_1 (out, and_1_out, and_2_out, and_3_out, and_4_out);

  // Other names for the same wires on the sheet: xsecond8[7:0] = x[7:0]; xbit2 = x[7]; xfirst8[7:0] = x[15:8];
  //   xbit1 = x[15]; ysecond8[7:0] = y[7:0]; ybit2 = y[7]; yfirst8[7:0] = y[15:8]; ybit1 = y[15]
endmodule
