// Logisim project cpu.circ as structural Verilog: 3 circuits, main circuit main
module main (
  input  [15:0] From_Instr_Mem,
  input  clk,
  output [15:0] r0,
  output [15:0] r1,
  output [15:0] r2,
  output [15:0] r3,
  output [15:0] Display_0,
  output [15:0] Display_1,
  output [15:0] To_Instr_Mem,
  output [15:0] Data_Mem_Data,
  output [15:0] Data_Mem_Addr,
  output Data_Mem_Write
);

  wire ALUCtr, ALUSrc, and_1_out, and_2_out, and_3_out, and_4_out, beq, bne, Branch, button_1_out,
       comparator_1_eq, comparator_2_eq, comparator_3_eq, disp, j, jal, jr, lui, main_1_signed_overflow,
       MemRead, MemtoReg, nop, not_1_out, not_2_out, or_1_out, or_3_out, RegDst, RegWr, shift, \unsigned ;
  wire [1:0] multiplexer_4_out, rd, rs, rt;
  wire [3:0] multiplexer_1_out, opcode;
  wire [5:0] funct;
  wire [7:0] imm;
  wire [11:0] taddress;
  wire [15:0] _0ext, adder_1_out, adder_2_out, DataOut, immresult, multiplexer_2_out, multiplexer_3_out,
       multiplexer_5_out, multiplexer_6_out, multiplexer_7_out, multiplexer_9_out, offset, RegData1,
       RegData2, register_3_q, shifter_1_out, WriteDataIn;

  control control_1 (
    .opcode(opcode), .beq(beq), .bne(bne), .disp(disp), .RegDst(RegDst), .RegWr(RegWr), .Branch(Branch),
    .ALUSrc(ALUSrc), .ALUCtr(ALUCtr), .MemWr(Data_Mem_Write), .MemRead(MemRead), .MemtoReg(MemtoReg),
    .jal(jal), .j(j), .jr(jr), .shift(shift), .\unsigned (\unsigned ), .lui(lui));
  Register #(.width(16)) register_1 (.D(multiplexer_5_out), .Q(To_Instr_Mem), .clk(clk));  // open: en, clr
  Adder #(.width(16)) adder_1 (.a(16'h1), .b(To_Instr_Mem), .out(adder_1_out));  // open: cin, cout
  Adder #(.width(16)) adder_2 (.a(To_Instr_Mem), .b(offset), .out(adder_2_out));  // open: cin, cout
  Multiplexer #(.select(4), .width(4), .enable("false")) multiplexer_1 (
    .in0(funct[3:0]), .in5(4'b0000), .in6(4'b0111), .in7(4'b0110), .in9(4'b0000), .in11(4'b0000),
    .out(multiplexer_1_out), .sel(opcode));  // open: in1, in2, in3, in4, in8, in10, in12, in13, in14, in15
  Comparator #(.width(16)) comparator_1 (.a(Data_Mem_Data), .b(RegData1), .eq(comparator_1_eq));  // open: gt, lt
  Multiplexer #(.width(16), .enable("false")) multiplexer_2 (
    .in0(adder_1_out), .in1(adder_2_out), .out(multiplexer_2_out), .sel(nop));
  alu_main main_1 (
    .Switch__S(multiplexer_1_out), .X(RegData1), .RESULT(Data_Mem_Addr),
    .Signed_Overflow(main_1_signed_overflow), .Y(RegData2));  // open: Equal
  LED led_1 (.in(main_1_signed_overflow));
  Multiplexer #(.width(16), .enable("false")) multiplexer_3 (
    .in0(multiplexer_2_out), .in1({To_Instr_Mem[15:12], taddress}), .out(multiplexer_3_out), .sel(or_1_out));
  or or_1 (or_1_out, j, jal);
  and and_1 (and_1_out, comparator_1_eq, beq);
  not not_1 (not_1_out, comparator_1_eq);
  and and_2 (and_2_out, not_1_out, bne);
  Multiplexer #(.select(4), .width(2), .enable("false")) multiplexer_4 (
    .in0(rd), .in1(2'b11), .in5(rt), .in6(rt), .in7(rt), .in10(rt), .in11(rt), .out(multiplexer_4_out),
    .sel(opcode));  // open: in2, in3, in4, in8, in9, in12, in13, in14, in15
  or or_2 (nop, and_1_out, and_2_out);
  Multiplexer #(.width(16), .enable("false")) multiplexer_5 (
    .in0(multiplexer_3_out), .in1(RegData1), .out(multiplexer_5_out), .sel(jr));
  Regfile_main main_2 (
    .Read_register_1(rs), .Read_register_2(rt), .write_register(multiplexer_4_out), .write_data(WriteDataIn),
    .Reg_0_Value(r0), .Reg_1_Value(r1), .Reg_2_Value(r2), .Reg_3_Value(r3), .RegWrite(RegWr), .clock(clk),
    .Read_Data_1(RegData1), .Read_Data_2(Data_Mem_Data));
  Comparator #(.width(16)) comparator_2 (.a(_0ext), .b({16{1'b0}}), .eq(comparator_2_eq));  // open: gt, lt
  assign DataOut = Data_Mem_Write ? Data_Mem_Data : 16'bz;  // Controlled_Buffer controlled_buffer_1
  not not_2 (not_2_out, Data_Mem_Write);
  Register #(.width(16)) register_2 (.D(RegData1), .en(and_3_out), .Q(Display_0), .clk(clk));  // open: clr
  and and_3 (and_3_out, disp, comparator_2_eq);
  assign offset = {{8{imm[7]}}, imm};  // Bit_Extender bit_extender_1
  assign _0ext = {{8{1'b0}}, imm};  // Bit_Extender bit_extender_2
  RAM #(.addrWidth(16), .dataWidth(16)) ram_1 (
    .addr(Data_Mem_Addr), .data(DataOut), .sel(1'b1), .clk(clk), .ld(not_2_out), .clr(button_1_out));
  Button button_1 (.out(button_1_out));
  Hex_Digit_Display hex_digit_display_1 (.value(Display_0[11:8]));  // open: dp
  Hex_Digit_Display hex_digit_display_2 (.value(Display_0[15:12]));  // open: dp
  Multiplexer #(.width(16), .enable("false")) multiplexer_6 (
    .in0(From_Instr_Mem), .in1(16'h6), .out(multiplexer_6_out), .sel(or_3_out));
  or or_3 (or_3_out, jal, j, jr, nop);
  Multiplexer #(.width(16), .enable("false")) multiplexer_7 (
    .in0(Data_Mem_Addr), .in1(DataOut), .out(multiplexer_7_out), .sel(MemtoReg));
  Multiplexer #(.width(16), .enable("false")) multiplexer_8 (
    .in0(offset), .in1(_0ext), .out(immresult), .sel(\unsigned ));
  Hex_Digit_Display hex_digit_display_3 (.value(Display_0[7:4]));  // open: dp
  Hex_Digit_Display hex_digit_display_4 (.value(Display_0[3:0]));  // open: dp
  Comparator #(.width(16)) comparator_3 (.a(_0ext), .b(16'h1), .eq(comparator_3_eq));  // open: gt, lt
  Register #(.width(16)) register_3 (.D(multiplexer_6_out), .Q(register_3_q), .clk(clk));  // open: en, clr
  Multiplexer #(.width(16), .enable("false")) multiplexer_9 (
    .in0(multiplexer_7_out), .in1(shifter_1_out), .out(multiplexer_9_out), .sel(lui));
  Multiplexer #(.width(16), .enable("false")) multiplexer_10 (
    .in0(Data_Mem_Data), .in1(immresult), .out(RegData2), .sel(shift));
  Hex_Digit_Display hex_digit_display_5 (.value(Display_1[15:12]));  // open: dp
  Register #(.width(16)) register_4 (.D(RegData1), .en(and_4_out), .Q(Display_1), .clk(clk));  // open: clr
  and and_4 (and_4_out, disp, comparator_3_eq);
  instrsplit instrsplit_1 (
    .in(register_3_q), .funct(funct), .rd(rd), .rt(rt), .rs(rs), .imm(imm), .address(taddress),
    .opcode(opcode));
  Shifter #(.width(16)) shifter_1 (.in(immresult), .\dist (4'b1000), .out(shifter_1_out));
  Hex_Digit_Display hex_digit_display_6 (.value(Display_1[7:4]));  // open: dp
  Hex_Digit_Display hex_digit_display_7 (.value(Display_1[11:8]));  // open: dp
  Multiplexer #(.width(16), .enable("false")) multiplexer_11 (
    .in0(multiplexer_9_out), .in1(To_Instr_Mem), .out(WriteDataIn), .sel(jal));
  Hex_Digit_Display hex_digit_display_8 (.value(Display_1[3:0]));  // open: dp

  // Other names for the same wires on the sheet: CurrentPC[15:0] = To_Instr_Mem; Address[15:0] = Data_Mem_Addr;
  //   d0[15:0] = Display_0; d1[15:0] = Display_1; DataIn[15:0] = Data_Mem_Data; Input[15:0] = From_Instr_Mem;
  //   MemWr = Data_Mem_Write

  // Notes on the sheet:
  //   This is the current PC that you need to send as OUTPUT
  //   This is the instruction that you would receive as INPUT
  //   This is a CLK that is an INPUT driven from the harness.
  //   Remember, this circuit is loaded from the harness to be tested!
  //   DO NOT CHANGE THE LOCATIONS OF THE INPUTS OR OUTPUTS! IF YOU DO SO, YOU NEED TO MAKE SURE THE PINS ARE IN THE RIGHT PLACES!
  //   These are OUTPUTS of the circuit
  //   These are OUTPUTS of the circuit
endmodule

module control (
  input  [3:0] opcode,
  output RegDst,
  output RegWr,
  output Branch,
  output ALUSrc,
  output ALUCtr,
  output beq,
  output MemWr,
  output bne,
  output MemRead,
  output disp,
  output MemtoReg,
  output jal,
  output j,
  output jr,
  output shift,
  output \unsigned ,
  output lui
);

  wire addi, andi, not_1_out, not_2_out, not_3_out, not_4_out, not_6_out, not_7_out, not_8_out, ori, rtype;

  Demultiplexer #(.select(4), .enable("false")) demultiplexer_1 (
    .out0(rtype), .out1(jal), .out2(j), .out3(jr), .out4(beq), .out5(addi), .out6(andi), .out7(ori),
    .out8(bne), .out9(MemWr), .out10(lui), .out11(MemRead), .out12(disp), .in(1'b1), .sel(opcode));  // open: out13, out14, out15
  not not_1 (not_1_out, jal);
  not not_2 (not_2_out, j);
  not not_3 (not_3_out, jr);
  not not_4 (not_4_out, rtype);
  not not_5 (RegDst, rtype);
  not not_6 (not_6_out, beq);
  not not_7 (not_7_out, bne);
  not not_8 (not_8_out, rtype);
  and and_1 (shift, not_1_out, not_2_out, not_3_out, not_4_out);
  or or_1 (\unsigned , andi, ori, lui, disp);
  or or_2 (Branch, beq, bne);
  and and_2 (ALUSrc, not_6_out, not_7_out, not_8_out);
  or or_3 (RegWr, jal, addi, andi, ori, lui, MemRead, rtype);
  or or_4 (ALUCtr, addi, andi, ori, MemWr, lui, MemRead, rtype);

  assign MemtoReg = MemRead;

  // Other names for the same wires on the sheet: lw = MemRead; sw = MemWr
endmodule

module instrsplit (
  input  [15:0] in,
  output [5:0] funct,
  output [1:0] rd,
  output [1:0] rt,
  output [1:0] rs,
  output [7:0] imm,
  output [11:0] address,
  output [3:0] opcode
);


  assign address = in[11:0];
  assign funct = in[5:0];
  assign imm = in[7:0];
  assign opcode = in[15:12];
  assign rd = in[7:6];
  assign rs = in[11:10];
  assign rt = in[9:8];
endmodule
